# Fritzing sketch SPI_comms (saved by Fritzing 1.0.3b)
breadboards: 1

parts:
  SheRhi_Arduino_Uno = Arduino Uno (Rev3)
  SheRhi_Raspberry_Pi = Raspberry Pi 4B

nets:
  N1: SheRhi_Arduino_Uno.D10_PWM/SS, SheRhi_Raspberry_Pi.GPIO8
  N2: SheRhi_Arduino_Uno.D11_PWM/MOSI, SheRhi_Raspberry_Pi.GPIO10
  N3: SheRhi_Arduino_Uno.D12/MISO, SheRhi_Raspberry_Pi.GPIO9
  N4: SheRhi_Arduino_Uno.D13/SCK, SheRhi_Raspberry_Pi.GPIO11
  GND: SheRhi_Arduino_Uno.GND, SheRhi_Raspberry_Pi.GND

notes:
  SPI Communications
  Master: SheRhi Raspberry Pi
  Slave: SheRhi Arudino Uno
